# Fritzing sketch circuit (saved by Fritzing 0.9.3b)
breadboards: 1

parts:
  U1 = Voltage Regulator - 5V [package="DPak [SMD]"]
  Power_plug1 = Power plug
  IR1 = TSOP312.., 314.. [package=THT]
  Q1 = MOSFET-NCHANNEL [package=dpak]
  Q2 = MOSFET-NCHANNEL [package=dpak]
  Q3 = MOSFET-NCHANNEL [package=dpak]
  Q4 = MOSFET-NCHANNEL [package=dpak]
  WeMos_D1_Mini1 = WeMos D1 Mini

nets:
  RGBW VCC: U1.input_voltage, Power_plug1.VCC
  GND: U1.GND, Power_plug1.GND, IR1.GND, Q1.S, Q2.S, Q3.S, Q4.S, WeMos_D1_Mini1.G
  N1: U1.output_voltage, IR1.Vs, WeMos_D1_Mini1.5V
  N2: IR1.Data, WeMos_D1_Mini1.D5
  N3: Q1.G, WeMos_D1_Mini1.D1
  RGBW Red: Q1.D
  N4: Q2.G, WeMos_D1_Mini1.D2
  RGBW Blue: Q2.D
  N5: Q3.G, WeMos_D1_Mini1.D0
  RGBW Green: Q3.D
  N6: Q4.G, WeMos_D1_Mini1.D6
  RGBW White: Q4.D
